# Fritzing sketch lpg_detection (saved by Fritzing 0.9.3b)

parts:
  Part1 = Arduino Uno (Rev3)
  Mod1 = KY-019 5V Relay Module [package="Breakout board"]
  VALVE1 = Plastic Solenoid Valve
  Part2 = MQ-4
  Power_plug1 = Power plug
  GSM_SIM_GPSR_SMS_SIM900_SIM1 = SIM800L [package=THT]
  J1 = Piezo Speaker
  LED1 = LED - 5mm [color="Red (633nm)" package="5 mm [THT]"]

nets:
  N1: Part1.A0, Part2.DO
  GND: Part1.D10_PWM/SS, Part1.GND, Mod1.+, Part2.AO, GSM_SIM_GPSR_SMS_SIM900_SIM1.SIM_RXD, GSM_SIM_GPSR_SMS_SIM900_SIM1.GND, J1.pin1, LED1.cathode
  N2: Part1.D11_PWM/MOSI, GSM_SIM_GPSR_SMS_SIM900_SIM1.SIM_TXD
  N3: Part1.D2, Mod1.S
  N4: Part1.D3_PWM, LED1.anode
  N5: Part1.D4, J1.pin2
  5V: Part1.5V, Mod1.-, Part2.VCC, GSM_SIM_GPSR_SMS_SIM900_SIM1.5V
  N6: Mod1.Common, Power_plug1.GND
  N7: Mod1.NO, VALVE1.no_name_yet#2
  N8: VALVE1.no_name_yet#1, Power_plug1.VCC

custom parts:
  KY-019 5V Relay Module: KY-019 5V Relay module, used to control AC circuits. (Special thanks to vanepp for fixing the PCB holes and other errors)
